// Logisim project synthesizer.circ as structural Verilog: 2 circuits, main circuit main
module main (
  input  in_1,
  input  Play
);

  wire A_h_out, A_out, and_1_out, B_h_out, B_out, button_1_out, button_2_out, button_3_out, button_4_out,
       button_5_out, button_6_out, button_7_out, button_8_out, button_9_out, button_10_out, C5_out, C_h_out,
       C_out, clock_1_out, clock_2_out, clock_3_out, clock_4_out, clock_5_out, clock_6_out, clock_7_out,
       clock_8_out, D_h_out, D_out, E_h_out, E_out, F_h_out, F_out, G_h_out, G_out, multiplexer_1_out,
       Reset_out;
  wire [2:0] Instrument1_out, Instrument2_out, Instrument3_out, Instrument4_out, Tempo_out;
  wire [4:0] rom_1_data;
  wire [6:0] counter_1_q;
  wire [7:0] controlled_buffer_1_out, controlled_buffer_26_out, controlled_buffer_27_out,
       controlled_buffer_28_out, demultiplexer_1_out0, demultiplexer_1_out1, demultiplexer_1_out2,
       demultiplexer_1_out3, demultiplexer_1_out4, demultiplexer_1_out5, demultiplexer_1_out6,
       demultiplexer_1_out7, demultiplexer_1_out8, demultiplexer_1_out9, demultiplexer_1_out10,
       demultiplexer_1_out11, demultiplexer_1_out12, demultiplexer_1_out13, demultiplexer_1_out14,
       demultiplexer_1_out15, demultiplexer_1_out16, demultiplexer_1_out17, demultiplexer_1_out18,
       demultiplexer_1_out19, demultiplexer_1_out20, demultiplexer_1_out21, demultiplexer_1_out22,
       demultiplexer_1_out23, demultiplexer_1_out24, Main_Melody_data, multiplexer_2_out, rom_2_data,
       rom_3_data, rom_4_data, sound_emitter_1_p5, sound_emitter_2_p5, sound_emitter_3_p5, sound_emitter_4_p5;

  Demultiplexer #(.select(5), .width(8)) demultiplexer_1 (
    .out0(demultiplexer_1_out0), .out1(demultiplexer_1_out1), .out2(demultiplexer_1_out2),
    .out3(demultiplexer_1_out3), .out4(demultiplexer_1_out4), .out5(demultiplexer_1_out5),
    .out6(demultiplexer_1_out6), .out7(demultiplexer_1_out7), .out8(demultiplexer_1_out8),
    .out9(demultiplexer_1_out9), .out10(demultiplexer_1_out10), .out11(demultiplexer_1_out11),
    .out12(demultiplexer_1_out12), .out13(demultiplexer_1_out13), .out14(demultiplexer_1_out14),
    .out15(demultiplexer_1_out15), .out16(demultiplexer_1_out16), .out17(demultiplexer_1_out17),
    .out18(demultiplexer_1_out18), .out19(demultiplexer_1_out19), .out20(demultiplexer_1_out20),
    .out21(demultiplexer_1_out21), .out22(demultiplexer_1_out22), .out23(demultiplexer_1_out23),
    .out24(demultiplexer_1_out24), .in({8{1'b1}}), .sel(rom_1_data));  // open: out25, out26, out27, out28, out29, out30, out31
  Clock #(.highDuration(32), .lowDuration(32), .phaseOffset(1)) clock_1 (.out(clock_1_out));
  Clock #(.highDuration(16), .lowDuration(16), .phaseOffset(1)) clock_2 (.out(clock_2_out));
  Clock #(.highDuration(8), .lowDuration(8)) clock_3 (.out(clock_3_out));
  Clock #(.highDuration(6), .lowDuration(6), .phaseOffset(1)) clock_4 (.out(clock_4_out));
  Clock #(.highDuration(5), .lowDuration(5), .phaseOffset(1)) clock_5 (.out(clock_5_out));
  Clock #(.highDuration(4), .lowDuration(4), .phaseOffset(1)) clock_6 (.out(clock_6_out));
  Clock #(.highDuration(2), .lowDuration(2), .phaseOffset(1)) clock_7 (.out(clock_7_out));
  Clock #(.phaseOffset(1)) clock_8 (.out(clock_8_out));
  Slider #(.width(3)) Tempo (.out(Tempo_out));
  DotMatrix #(.dotshape("circle"), .inputtype("row"), .matrixcols(8), .matrixrows(25)) dotmatrix_1 (
    .row0(demultiplexer_1_out0), .row1(demultiplexer_1_out1), .row2(demultiplexer_1_out2),
    .row3(demultiplexer_1_out3), .row4(demultiplexer_1_out4), .row5(demultiplexer_1_out5),
    .row6(demultiplexer_1_out6), .row7(demultiplexer_1_out7), .row8(demultiplexer_1_out8),
    .row9(demultiplexer_1_out9), .row10(demultiplexer_1_out10), .row11(demultiplexer_1_out11),
    .row12(demultiplexer_1_out12), .row13(demultiplexer_1_out13), .row14(demultiplexer_1_out14),
    .row15(demultiplexer_1_out15), .row16(demultiplexer_1_out16), .row17(demultiplexer_1_out17),
    .row18(demultiplexer_1_out18), .row19(demultiplexer_1_out19), .row20(demultiplexer_1_out20),
    .row21(demultiplexer_1_out21), .row22(demultiplexer_1_out22), .row23(demultiplexer_1_out23),
    .row24(demultiplexer_1_out24));
  Button C (.out(C_out));
  assign controlled_buffer_1_out = C_out ? 8'h3c : 8'bz;  // Controlled_Buffer controlled_buffer_1
  Multiplexer #(.select(3)) multiplexer_1 (
    .in0(clock_1_out), .in1(clock_2_out), .in2(clock_3_out), .in3(clock_4_out), .in4(clock_5_out),
    .in5(clock_6_out), .in6(clock_7_out), .in7(clock_8_out), .out(multiplexer_1_out), .sel(Tempo_out));
  assign controlled_buffer_1_out = button_1_out ? 8'h3d : 8'bz;  // Controlled_Buffer controlled_buffer_2
  assign controlled_buffer_1_out = button_2_out ? 8'h3f : 8'bz;  // Controlled_Buffer controlled_buffer_3
  Button button_1 (.out(button_1_out));
  Button button_2 (.out(button_2_out));
  Button D (.out(D_out));
  Button E (.out(E_out));
  assign controlled_buffer_1_out = D_out ? 8'h3e : 8'bz;  // Controlled_Buffer controlled_buffer_4
  assign controlled_buffer_1_out = E_out ? 8'h40 : 8'bz;  // Controlled_Buffer controlled_buffer_5
  Button Reset (.out(Reset_out));
  ROM #(.dataWidth(5)) rom_1 (.addr(Main_Melody_data), .data(rom_1_data));
  assign controlled_buffer_1_out = button_3_out ? 8'h42 : 8'bz;  // Controlled_Buffer controlled_buffer_6
  Button button_3 (.out(button_3_out));
  Button F (.out(F_out));
  assign controlled_buffer_1_out = F_out ? 8'h41 : 8'bz;  // Controlled_Buffer controlled_buffer_7
  Counter #(.max('h7f), .ongoal("stay"), .width(7)) counter_1 (
    .clr(Reset_out), .load(1'b0), .up(1'b1), .clk(and_1_out), .Q(counter_1_q));  // open: count, D, carry
  and and_1 (and_1_out, Play, multiplexer_1_out);
  assign controlled_buffer_1_out = button_4_out ? 8'h44 : 8'bz;  // Controlled_Buffer controlled_buffer_8
  Button button_4 (.out(button_4_out));
  Button G (.out(G_out));
  Button A (.out(A_out));
  assign controlled_buffer_1_out = G_out ? 8'h43 : 8'bz;  // Controlled_Buffer controlled_buffer_9
  assign controlled_buffer_1_out = A_out ? 8'h45 : 8'bz;  // Controlled_Buffer controlled_buffer_10
  assign controlled_buffer_1_out = button_5_out ? 8'h46 : 8'bz;  // Controlled_Buffer controlled_buffer_11
  Button button_5 (.out(button_5_out));
  Button B (.out(B_out));
  assign controlled_buffer_1_out = B_out ? 8'h47 : 8'bz;  // Controlled_Buffer controlled_buffer_12
  assign controlled_buffer_1_out = button_6_out ? 8'h49 : 8'bz;  // Controlled_Buffer controlled_buffer_13
  Button button_6 (.out(button_6_out));
  Button C_h (.out(C_h_out));
  assign controlled_buffer_1_out = C_h_out ? 8'h48 : 8'bz;  // Controlled_Buffer controlled_buffer_14
  assign controlled_buffer_1_out = D_h_out ? 8'h4a : 8'bz;  // Controlled_Buffer controlled_buffer_15
  ROM #(.addrWidth(7)) Main_Melody (.addr(counter_1_q), .data(Main_Melody_data));
  ROM #(.addrWidth(7)) rom_2 (.addr(counter_1_q), .data(rom_2_data));
  ROM #(.addrWidth(7)) rom_3 (.addr(counter_1_q), .data(rom_3_data));
  ROM #(.addrWidth(7)) rom_4 (.addr(counter_1_q), .data(rom_4_data));
  assign controlled_buffer_1_out = button_7_out ? 8'h4b : 8'bz;  // Controlled_Buffer controlled_buffer_16
  Button button_7 (.out(button_7_out));
  Button E_h (.out(E_h_out));
  Button D_h (.out(D_h_out));
  assign controlled_buffer_1_out = E_h_out ? 8'h4c : 8'bz;  // Controlled_Buffer controlled_buffer_17
  Button F_h (.out(F_h_out));
  assign controlled_buffer_1_out = F_h_out ? 8'h4d : 8'bz;  // Controlled_Buffer controlled_buffer_18
  assign controlled_buffer_1_out = button_9_out ? 8'h50 : 8'bz;  // Controlled_Buffer controlled_buffer_19
  assign controlled_buffer_1_out = button_8_out ? 8'h4e : 8'bz;  // Controlled_Buffer controlled_buffer_20
  Button button_8 (.out(button_8_out));
  Button button_9 (.out(button_9_out));
  Button G_h (.out(G_h_out));
  assign controlled_buffer_1_out = G_h_out ? 8'h4f : 8'bz;  // Controlled_Buffer controlled_buffer_21
  assign controlled_buffer_1_out = A_h_out ? 8'h51 : 8'bz;  // Controlled_Buffer controlled_buffer_22
  Controlled_Buffer #(.width(8)) controlled_buffer_23 (.in(8'h52), .en(button_10_out));  // open: out
  Button button_10 (.out(button_10_out));
  Button A_h (.out(A_h_out));
  Button B_h (.out(B_h_out));
  assign controlled_buffer_1_out = B_h_out ? 8'h53 : 8'bz;  // Controlled_Buffer controlled_buffer_24
  Button C5 (.out(C5_out));
  assign controlled_buffer_1_out = C5_out ? 8'h54 : 8'bz;  // Controlled_Buffer controlled_buffer_25
  Multiplexer #(.width(8)) multiplexer_2 (
    .in0(controlled_buffer_1_out), .in1(Main_Melody_data), .out(multiplexer_2_out), .sel(in_1));
  assign controlled_buffer_26_out = in_1 ? rom_2_data : 8'bz;  // Controlled_Buffer controlled_buffer_26
  assign controlled_buffer_27_out = in_1 ? rom_4_data : 8'bz;  // Controlled_Buffer controlled_buffer_27
  assign controlled_buffer_28_out = in_1 ? rom_3_data : 8'bz;  // Controlled_Buffer controlled_buffer_28
  // sound_emitter sound_emitter_1: pin names not known; wires that end beside it: 4'b0001, 1'b1, controlled_buffer_27_out, 7'b0111100, sound_emitter_1_p5
  // sound_emitter sound_emitter_2: pin names not known; wires that end beside it: 4'b0000, 1'b1, multiplexer_2_out, 7'b0111100, sound_emitter_2_p5
  // sound_emitter sound_emitter_3: pin names not known; wires that end beside it: 4'b0001, 1'b1, controlled_buffer_26_out, 7'b0111100, sound_emitter_3_p5
  // sound_emitter sound_emitter_4: pin names not known; wires that end beside it: 4'b0001, 1'b1, controlled_buffer_28_out, 7'b0111100, sound_emitter_4_p5
  Slider #(.width(3)) Instrument1 (.out(Instrument1_out));
  Slider #(.width(3)) Instrument2 (.out(Instrument2_out));
  Slider #(.width(3)) Instrument3 (.out(Instrument3_out));
  Slider #(.width(3)) Instrument4 (.out(Instrument4_out));
  ROM #(.addrWidth(3)) rom_5 (.addr(Instrument1_out), .data(sound_emitter_2_p5));
  ROM #(.addrWidth(3)) rom_6 (.addr(Instrument2_out), .data(sound_emitter_3_p5));
  ROM #(.addrWidth(3)) rom_7 (.addr(Instrument3_out), .data(sound_emitter_4_p5));
  ROM #(.addrWidth(3)) rom_8 (.addr(Instrument4_out), .data(sound_emitter_1_p5));

  // Notes on the sheet:
  //   Slow
  //   Keybord
  //   Fast
  //   Note Display
  //   contents of rom_1 (hex, n*v repeats v):
  //   60*19 0 1 2 3 4 5 6 7 8 9 a b c d e f 10 11 12 13 14 15 16 17 18 171*19
  //   contents of Main_Melody (hex, n*v repeats v):
  //   40 48 48 80 40 47 47 80 40 45 45 43 41 43 43 3c 3e 41 45 48 47 43 40 3e 4*40 4*80 40 48 48 80 40 47
  //   47 80 40 45 45 43 41 43 80 40 3e 41 45 48 4a 4c 47 43 4*45 4*80 40 48 48 80 40 47 47 80 40 45 45 43
  //   41 43 43 3c 3e 41 45 48 47 43 40 3e 4*40 4*80 40 48 48 80 40 47 47 80 40 45 45 43 41 43 80 40 3e 41
  //   45 48 4a 4c 47 43 4*45 4*80
  //   contents of rom_2 (hex, n*v repeats v):
  //   80 40 40 80 80 3e 3e 80 80 3c 3c 80 80 3e 3e 5*80 43 80 80 80 4*3c 5*80 40 40 80 80 3e 3e 80 80 3c
  //   3c 80 80 3e 6*80 47 80 80 80 4*40 5*80 40 40 80 80 3e 3e 80 80 3c 3c 80 80 3e 3e 5*80 43 80 80 80
  //   4*3c 5*80 40 40 80 80 3e 3e 80 80 3c 3c 80 80 3e 6*80 47 80 80 80 4*40 4*80
  //   contents of rom_3 (hex, n*v repeats v):
  //   80 45 45 80 80 43 43 80 80 41 41 80 80 3c 3c 80 4*3e 4*43 4*40 5*80 45 45 80 80 43 43 80 80 41 41 80
  //   80 3c 3c 80 4*3e 4*43 4*40 5*80 45 45 80 80 43 43 80 80 41 41 80 80 3c 3c 80 4*3e 4*43 4*40 5*80 45
  //   45 80 80 43 43 80 80 41 41 80 80 3c 3c 80 4*3e 4*43 4*40 4*80
  //   contents of rom_4 (hex, n*v repeats v):
  //   80 3c 3c 80 80 3e 3e 80 80 3c 3c 80 80 3c 3c 80 4*41 4*3e 4*3c 5*80 3c 3c 80 80 3e 3e 80 80 3c 3c 80
  //   80 3c 3c 80 4*41 4*3e 4*3c 5*80 3c 3c 80 80 3e 3e 80 80 3c 3c 80 80 3c 3c 80 4*41 4*3e 4*3c 5*80 3c
  //   3c 80 80 3e 3e 80 80 3c 3c 80 80 3c 3c 80 4*41 4*3e 4*3c 4*80
  //   contents of rom_5 (hex, n*v repeats v):
  //   0 1 8 18 28 38 40 49
  //   contents of rom_6 (hex, n*v repeats v):
  //   0 1 8 18 28 38 40 49
  //   contents of rom_7 (hex, n*v repeats v):
  //   0 1 8 18 28 38 40 49
  //   contents of rom_8 (hex, n*v repeats v):
  //   0 1 8 18 28 38 40 49
  //   0: Piano
  //   1: Bright Piano
  //   8:Celesta
  //   18: Rock Organ
  //   40: Violin
  //   28: Electric Guitar
  //   38: AcousticBass
  //   49: String Ensemble
endmodule

module Animator (
  input  Clk,
  output [7:0] X,
  output [7:0] Y,
  output [3:0] Color,
  output WriteEnable
);

  wire clock_1_out, comparator_1_eq, comparator_2_eq;
  wire [1:0] counter_3_q;
  wire [5:0] counter_1_q;
  wire [7:0] adder_1_out, bit_extender_1_out, bit_extender_2_out, multiplier_1_out;
  wire [7:4] rom_1_data;
  wire [15:0] counter_2_q;

  Clock clock_1 (.out(clock_1_out));
  Counter #(.max('h38), .width(6)) counter_1 (
    .clk(clock_1_out), .Q(counter_1_q));  // open: clr, load, up, count, D, carry
  Counter #(.max('hffff), .width(16)) counter_2 (
    .clr(comparator_1_eq), .clk(clock_1_out), .Q(counter_2_q));  // open: load, up, count, D, carry
  assign bit_extender_1_out = {{2{1'b0}}, counter_1_q};  // Bit_Extender bit_extender_1
  Counter #(.max('h2), .width(2)) counter_3 (
    .clk(comparator_1_eq), .Q(counter_3_q));  // open: clr, load, up, count, D, carry
  Comparator #(.width(16)) comparator_1 (.a(16'h10), .b(counter_2_q), .eq(comparator_1_eq));  // open: gt, lt
  assign bit_extender_2_out = {{6{1'b0}}, counter_3_q};  // Bit_Extender bit_extender_2
  Multiplier multiplier_1 (.a(bit_extender_2_out), .b(8'h39), .out(multiplier_1_out));  // open: cin, cout
  Adder adder_1 (.a(multiplier_1_out), .b(bit_extender_1_out), .out(adder_1_out));  // open: cin, cout
  ROM #(.dataWidth(16)) rom_1 (.addr(adder_1_out), .data({X, rom_1_data, Color}));
  assign Y = {{4{1'b0}}, rom_1_data};  // Bit_Extender bit_extender_3
  not not_1 (WriteEnable, comparator_2_eq);
  Comparator #(.width(16)) comparator_2 (
    .a({X, rom_1_data, Color}), .b({16{1'b1}}), .eq(comparator_2_eq));  // open: gt, lt

  // Notes on the sheet:
  //   contents of rom_1 (hex, n*v repeats v):
  //   80a 90a a0a b0a 80e 90e a0e b0e 912 a12 1c0a 1d0a 1e0a 1f0a 1c0e 1d0e 1e0e 1f0e 1d12 1e12 61a 71a
  //   201a 211a 51e 221e 522 2222 526 2226 52a 222a 52e 222e 532 2232 536 2236 53a 223a 53e 223e 542 2242
  //   546 2246 64a 74a 204a 214a c2a d2a e2a c2e d2e e2e 192a 1a2a 1b2a 192e 1a2e 1b2e 1236 1336 1436 1536
  //   133a 143a 113e 123e 153e 163e 1242 1342 1442 1542 84e 1f4e 752 2052 756 2056 75a 205a 75e 205e 762
  //   2062 766 2066 76a 206a 76e 206e 772 2072 776 2076 77a 207a 77e 207e 782 2082 786 2086 78a 208a 88e
  //   1f8e a92 b92 c92 d92 1092 1192 1292 1392 1492 1592 1692 1792 1a92 1b92 1c92 1d92 a96 b96 c96 d96
  //   1096 1196 1296 1396 1496 1596 1696 1796 1a96 1b96 1c96 1d96 a9a b9a c9a d9a 109a 119a 129a 139a 149a
  //   159a 169a 179a 1a9a 1b9a 1c9a 1d9a a9e b9e c9e d9e 109e 119e 129e 139e 149e 159e 169e 179e 1a9e 1b9e
  //   1c9e 1d9e 213e 223e 233e 2242 2342 2442 2346 2446 2546 244a 254a 264a 254e 264e 274e 2652 2752 2656
  //   2756 255a 265a 275a 245e 255e 265e 2362 2462 2562 2266 2366 2466 8000 213f 223f 233f 2243 2343 2443
  //   2347 2447 2547 8000 223b 233b 243b 233f 243f 253f 2443 2543 2643 8000 2337 2437 2537 243b 253b 263b
  //   253f 263f 273f 8000 213f 223f 233f 2243 2343 2443 2347 2447 2547 8000
endmodule
